// Logisim project curcuit.circ as structural Verilog: 4 circuits, main circuit CPU
module CPU (
);

  wire ALU_calc, ALU_out, cpu_clock, instruction_decoder_1_ir_i, instruction_decoder_1_ir_o, jump, num1_in,
       num1_out, num2_in, num2_out, or_1_out, PC_out, PC_up, R0_in, R0_out, R1_in, R1_out, R2_in, R2_out,
       RAM_adr_in, RAM_in, RAM_out, reset, reset_SBC;
  wire [2:0] alu_1_carry_out, bit_extender_5_out, CPU_flaga;
  wire [3:0] ALU_inst;
  wire [8:0] register_6_q_2;
  wire [15:0] bit_extender_1_out, bit_extender_3_out, programcounter_1_ip, programcounter_2_ip, register_1_q;
  wire [22:0] register_6_q;
  wire [31:0] alu_1_num_out, ALU_out_q, bit_extender_2_out, bit_extender_4_out, multiplexer_1_out, num2_q,
       ram_1_dout, register_2_q, register_3_q, register_4_q, register_5_q;

  LedBar #(.matrixcols(32)) ledbar_1 (
    .led0(bit_extender_2_out[31]), .led1(bit_extender_2_out[30]), .led2(bit_extender_2_out[29]),
    .led3(bit_extender_2_out[28]), .led4(bit_extender_2_out[27]), .led5(bit_extender_2_out[26]),
    .led6(bit_extender_2_out[25]), .led7(bit_extender_2_out[24]), .led8(bit_extender_2_out[23]),
    .led9(bit_extender_2_out[22]), .led10(bit_extender_2_out[21]), .led11(bit_extender_2_out[20]),
    .led12(bit_extender_2_out[19]), .led13(bit_extender_2_out[18]), .led14(bit_extender_2_out[17]),
    .led15(bit_extender_2_out[16]), .led16(bit_extender_2_out[15]), .led17(bit_extender_2_out[14]),
    .led18(bit_extender_2_out[13]), .led19(bit_extender_2_out[12]), .led20(bit_extender_2_out[11]),
    .led21(bit_extender_2_out[10]), .led22(bit_extender_2_out[9]), .led23(bit_extender_2_out[8]),
    .led24(bit_extender_2_out[7]), .led25(bit_extender_2_out[6]), .led26(bit_extender_2_out[5]),
    .led27(bit_extender_2_out[4]), .led28(bit_extender_2_out[3]), .led29(bit_extender_2_out[2]),
    .led30(bit_extender_2_out[1]), .led31(bit_extender_2_out[0]));
  Clock #(.phaseOffset(1)) clock_1 (.out(cpu_clock));
  Button button_1 (.out(reset));
  Register #(.width(16)) register_1 (
    .D(bit_extender_3_out), .en(RAM_adr_in), .clk(cpu_clock), .Q(register_1_q), .clr(reset));
  RAM #(.addrWidth(16), .dataWidth(32)) ram_1 (
    .addr(register_1_q), .we(RAM_in), .oe(RAM_out), .clk(cpu_clock), .din(multiplexer_1_out),
    .dout(ram_1_dout));
  Bit_Extender #(.in_width(32), .\type ("zero")) bit_extender_1 (.in(multiplexer_1_out), .out(bit_extender_1_out));
  ProgramCounter programcounter_1 (
    .JmpAddr(bit_extender_1_out), .Reset(reset), .Jmp(jump), .Clock(PC_up), .ip(programcounter_1_ip));
  assign bit_extender_2_out = {{16{programcounter_1_ip[15]}}, programcounter_1_ip};  // Bit_Extender bit_extender_2
  Bit_Extender #(.in_width(32), .\type ("zero")) bit_extender_3 (.in(multiplexer_1_out), .out(bit_extender_3_out));
  Multiplexer #(.width(32)) multiplexer_1 (
    .in1(bit_extender_2_out), .out(multiplexer_1_out), .sel(PC_out));  // open: in0
  Multiplexer #(.width(32)) multiplexer_2 (.in1(ram_1_dout), .out(multiplexer_1_out), .sel(RAM_out));  // open: in0
  LedBar #(.matrixcols(32)) ledbar_2 (
    .led0(multiplexer_1_out[31]), .led1(multiplexer_1_out[30]), .led2(multiplexer_1_out[29]),
    .led3(multiplexer_1_out[28]), .led4(multiplexer_1_out[27]), .led5(multiplexer_1_out[26]),
    .led6(multiplexer_1_out[25]), .led7(multiplexer_1_out[24]), .led8(multiplexer_1_out[23]),
    .led9(multiplexer_1_out[22]), .led10(multiplexer_1_out[21]), .led11(multiplexer_1_out[20]),
    .led12(multiplexer_1_out[19]), .led13(multiplexer_1_out[18]), .led14(multiplexer_1_out[17]),
    .led15(multiplexer_1_out[16]), .led16(multiplexer_1_out[15]), .led17(multiplexer_1_out[14]),
    .led18(multiplexer_1_out[13]), .led19(multiplexer_1_out[12]), .led20(multiplexer_1_out[11]),
    .led21(multiplexer_1_out[10]), .led22(multiplexer_1_out[9]), .led23(multiplexer_1_out[8]),
    .led24(multiplexer_1_out[7]), .led25(multiplexer_1_out[6]), .led26(multiplexer_1_out[5]),
    .led27(multiplexer_1_out[4]), .led28(multiplexer_1_out[3]), .led29(multiplexer_1_out[2]),
    .led30(multiplexer_1_out[1]), .led31(multiplexer_1_out[0]));
  Multiplexer #(.width(32)) multiplexer_3 (.in1(register_2_q), .out(multiplexer_1_out), .sel(num1_out));  // open: in0
  Multiplexer #(.width(32)) multiplexer_4 (.in1(register_3_q), .out(multiplexer_1_out), .sel(R0_out));  // open: in0
  Multiplexer #(.width(32)) multiplexer_5 (.in1(register_4_q), .out(multiplexer_1_out), .sel(R1_out));  // open: in0
  Multiplexer #(.width(32)) multiplexer_6 (.in1(register_5_q), .out(multiplexer_1_out), .sel(R2_out));  // open: in0
  Register #(.width(32)) register_2 (
    .D(multiplexer_1_out), .en(num1_in), .clk(cpu_clock), .Q(register_2_q), .clr(reset));
  Multiplexer #(.width(32)) multiplexer_7 (.in1(num2_q), .out(multiplexer_1_out), .sel(num2_out));  // open: in0
  Register #(.width(32)) num2 (.D(multiplexer_1_out), .en(num2_in), .clk(cpu_clock), .Q(num2_q), .clr(reset));
  Register #(.width(32)) register_3 (.D(multiplexer_1_out), .en(R0_in), .clk(cpu_clock), .Q(register_3_q), .clr(reset));
  Register #(.width(32)) register_4 (.D(multiplexer_1_out), .en(R1_in), .clk(cpu_clock), .Q(register_4_q), .clr(reset));
  Register #(.width(32)) register_5 (.D(multiplexer_1_out), .en(R2_in), .clk(cpu_clock), .Q(register_5_q), .clr(reset));
  LedBar #(.matrixcols(32)) ledbar_3 (
    .led0(num2_q[31]), .led1(num2_q[30]), .led2(num2_q[29]), .led3(num2_q[28]), .led4(num2_q[27]),
    .led5(num2_q[26]), .led6(num2_q[25]), .led7(num2_q[24]), .led8(num2_q[23]), .led9(num2_q[22]),
    .led10(num2_q[21]), .led11(num2_q[20]), .led12(num2_q[19]), .led13(num2_q[18]), .led14(num2_q[17]),
    .led15(num2_q[16]), .led16(num2_q[15]), .led17(num2_q[14]), .led18(num2_q[13]), .led19(num2_q[12]),
    .led20(num2_q[11]), .led21(num2_q[10]), .led22(num2_q[9]), .led23(num2_q[8]), .led24(num2_q[7]),
    .led25(num2_q[6]), .led26(num2_q[5]), .led27(num2_q[4]), .led28(num2_q[3]), .led29(num2_q[2]),
    .led30(num2_q[1]), .led31(num2_q[0]));
  LedBar #(.matrixcols(32)) ledbar_4 (
    .led0(register_2_q[31]), .led1(register_2_q[30]), .led2(register_2_q[29]), .led3(register_2_q[28]),
    .led4(register_2_q[27]), .led5(register_2_q[26]), .led6(register_2_q[25]), .led7(register_2_q[24]),
    .led8(register_2_q[23]), .led9(register_2_q[22]), .led10(register_2_q[21]), .led11(register_2_q[20]),
    .led12(register_2_q[19]), .led13(register_2_q[18]), .led14(register_2_q[17]), .led15(register_2_q[16]),
    .led16(register_2_q[15]), .led17(register_2_q[14]), .led18(register_2_q[13]), .led19(register_2_q[12]),
    .led20(register_2_q[11]), .led21(register_2_q[10]), .led22(register_2_q[9]), .led23(register_2_q[8]),
    .led24(register_2_q[7]), .led25(register_2_q[6]), .led26(register_2_q[5]), .led27(register_2_q[4]),
    .led28(register_2_q[3]), .led29(register_2_q[2]), .led30(register_2_q[1]), .led31(register_2_q[0]));
  Multiplexer #(.width(32)) multiplexer_8 (
    .in1(bit_extender_4_out), .out(multiplexer_1_out), .sel(instruction_decoder_1_ir_o));  // open: in0
  Register #(.width(32)) register_6 (
    .D(multiplexer_1_out), .en(instruction_decoder_1_ir_i), .clk(cpu_clock),
    .Q({register_6_q, register_6_q_2}), .clr(reset));
  ALU alu_1 (
    .instruction(ALU_inst), .num1(register_2_q), .num2(num2_q), .borrow_in(1'b0), .carry_in(1'b0),
    .mul_carry_in({32{1'b0}}), .div_upper({32{1'b0}}), .carry_out(alu_1_carry_out[0]),
    .borrow_out(alu_1_carry_out[1]), .comp_out(alu_1_carry_out[2]), .num_out(alu_1_num_out));
  assign bit_extender_4_out = {{9{1'b0}}, register_6_q};  // Bit_Extender bit_extender_4
  LedBar #(.matrixcols(32)) ledbar_5 (
    .led0(register_6_q[22]), .led1(register_6_q[21]), .led2(register_6_q[20]), .led3(register_6_q[19]),
    .led4(register_6_q[18]), .led5(register_6_q[17]), .led6(register_6_q[16]), .led7(register_6_q[15]),
    .led8(register_6_q[14]), .led9(register_6_q[13]), .led10(register_6_q[12]), .led11(register_6_q[11]),
    .led12(register_6_q[10]), .led13(register_6_q[9]), .led14(register_6_q[8]), .led15(register_6_q[7]),
    .led16(register_6_q[6]), .led17(register_6_q[5]), .led18(register_6_q[4]), .led19(register_6_q[3]),
    .led20(register_6_q[2]), .led21(register_6_q[1]), .led22(register_6_q[0]), .led23(register_6_q_2[8]),
    .led24(register_6_q_2[7]), .led25(register_6_q_2[6]), .led26(register_6_q_2[5]),
    .led27(register_6_q_2[4]), .led28(register_6_q_2[3]), .led29(register_6_q_2[2]),
    .led30(register_6_q_2[1]), .led31(register_6_q_2[0]));
  Register #(.width(3)) register_7 (.D(alu_1_carry_out), .en(ALU_calc), .clk(cpu_clock), .Q(CPU_flaga), .clr(reset));
  Multiplexer #(.width(32)) multiplexer_9 (.in1(ALU_out_q), .out(multiplexer_1_out), .sel(ALU_out));  // open: in0
  Register #(.width(32)) u_ALU_out (.D(alu_1_num_out), .en(ALU_calc), .clk(cpu_clock), .Q(ALU_out_q), .clr(reset));
  or or_1 (or_1_out, reset_SBC, reset);
  LedBar #(.matrixcols(32)) ledbar_6 (
    .led0(ALU_out_q[31]), .led1(ALU_out_q[30]), .led2(ALU_out_q[29]), .led3(ALU_out_q[28]),
    .led4(ALU_out_q[27]), .led5(ALU_out_q[26]), .led6(ALU_out_q[25]), .led7(ALU_out_q[24]),
    .led8(ALU_out_q[23]), .led9(ALU_out_q[22]), .led10(ALU_out_q[21]), .led11(ALU_out_q[20]),
    .led12(ALU_out_q[19]), .led13(ALU_out_q[18]), .led14(ALU_out_q[17]), .led15(ALU_out_q[16]),
    .led16(ALU_out_q[15]), .led17(ALU_out_q[14]), .led18(ALU_out_q[13]), .led19(ALU_out_q[12]),
    .led20(ALU_out_q[11]), .led21(ALU_out_q[10]), .led22(ALU_out_q[9]), .led23(ALU_out_q[8]),
    .led24(ALU_out_q[7]), .led25(ALU_out_q[6]), .led26(ALU_out_q[5]), .led27(ALU_out_q[4]),
    .led28(ALU_out_q[3]), .led29(ALU_out_q[2]), .led30(ALU_out_q[1]), .led31(ALU_out_q[0]));
  LedBar #(.matrixcols(3)) ledbar_7 (
    .led0(bit_extender_5_out[2]), .led1(bit_extender_5_out[1]), .led2(bit_extender_5_out[0]));
  Bit_Extender #(.in_width(16), .out_width(3)) bit_extender_5 (.in(programcounter_2_ip), .out(bit_extender_5_out));
  ProgramCounter programcounter_2 (
    .JmpAddr({16{1'b0}}), .Reset(or_1_out), .Jmp(1'b0), .Clock(cpu_clock), .ip(programcounter_2_ip));
  instruction_decoder instruction_decoder_1 (
    .instruction(register_6_q_2), .sub_stage(bit_extender_5_out), .carry(CPU_flaga[0]),
    .barrow(CPU_flaga[1]), .comp(CPU_flaga[2]), .RSC(reset_SBC), .MA_In(RAM_adr_in), .M_I(RAM_in),
    .M_O(RAM_out), .IR_I(instruction_decoder_1_ir_i), .IR_O(instruction_decoder_1_ir_o), .PC_O(PC_out),
    .PC_Up(PC_up), .PC_jmp(jump), .ALU_inst(ALU_inst), .A_I(ALU_calc), .A_O(ALU_out), .N1_I(num1_in),
    .N1_O(num1_out), .N2_I(num2_in), .N2_O(num2_out), .R0I(R0_in), .R0O(R0_out), .R1I(R1_in), .R1O(R1_out),
    .R2I(R2_in), .R2O(R2_out));
endmodule

module ProgramCounter (
  input  [15:0] JmpAddr,
  input  Reset,
  input  Jmp,
  input  Clock,
  output [15:0] ip
);

  wire [15:0] adder_1_out, multiplexer_1_out;

  Adder #(.width(16)) adder_1 (.a(ip), .b(16'h1), .out(adder_1_out));  // open: cin, cout
  Multiplexer #(.width(16)) multiplexer_1 (.in0(adder_1_out), .in1(JmpAddr), .out(multiplexer_1_out), .sel(Jmp));
  Register #(.width(16)) register_1 (.D(multiplexer_1_out), .en(1'b1), .Q(ip), .clk(Clock), .clr(Reset));
endmodule

module ALU (
  input  [3:0] instruction,
  input  [31:0] num1,
  input  [31:0] num2,
  input  borrow_in,
  input  carry_in,
  input  [31:0] mul_carry_in,
  input  [31:0] div_upper,
  output carry_out,
  output borrow_out,
  output comp_out,
  output [31:0] num_out
);

  wire comparator_1_eq, comparator_1_gt, comparator_1_lt, comparator_2_eq, comparator_2_gt, comparator_2_lt,
       fpcomparator_1_p3, fpcomparator_1_p4, fpcomparator_1_p5;
  wire [31:0] adder_1_out, divider_1_out, divider_2_out, fpadder_1_out, fpdivider_1_out, fpmultiplier_1_out,
       fpnegator_1_p2, fpsubtractor_1_out, fptoint_1_p2, inttofp_1_p2, inttofp_2_p2, multiplier_1_out,
       multiplier_2_out, negator_1_out, subtractor_1_out;

  Adder #(.width(32)) adder_1 (.a(num2), .b(num1), .out(adder_1_out), .cin(carry_in), .cout(carry_out));
  Subtractor #(.width(32)) subtractor_1 (
    .a(num2), .b(num1), .out(subtractor_1_out), .bin(borrow_in), .bout(borrow_out));
  Multiplier #(.width(32)) multiplier_1 (.a(num2), .b(num1), .out(multiplier_1_out), .cin(mul_carry_in));  // open: cout
  Multiplier #(.mode("twosComplement"), .width(32)) multiplier_2 (
    .a(num2), .b(num1), .out(multiplier_2_out), .cin(mul_carry_in));  // open: cout
  Divider #(.width(32)) divider_1 (.a(num2), .b(num1), .out(divider_1_out), .upper(div_upper));  // open: rem
  Divider #(.mode("twosComplement"), .width(32)) divider_2 (
    .a(num2), .b(num1), .out(divider_2_out), .upper(div_upper));  // open: rem
  Negator #(.width(32)) negator_1 (.in(num1), .out(negator_1_out));
  // IntToFP #(.mode("unsigned"), .width(32)) inttofp_1: pin names not known; wires that end beside it: num1, inttofp_1_p2
  // IntToFP #(.width(32)) inttofp_2: pin names not known; wires that end beside it: num1, inttofp_2_p2
  // FPToInt #(.width(32)) fptoint_1: pin names not known; wires that end beside it: num1, fptoint_1_p2
  Comparator #(.mode("unsigned"), .width(32)) comparator_1 (
    .a(num2), .b(num1), .gt(comparator_1_gt), .eq(comparator_1_eq), .lt(comparator_1_lt));
  Comparator #(.width(32)) comparator_2 (
    .a(num2), .b(num1), .gt(comparator_2_gt), .eq(comparator_2_eq), .lt(comparator_2_lt));
  // FPComparator fpcomparator_1: pin names not known; wires that end beside it: num2, num1, fpcomparator_1_p3, fpcomparator_1_p4, fpcomparator_1_p5
  FPAdder fpadder_1 (.a(num2), .b(num1), .out(fpadder_1_out));
  FPSubtractor fpsubtractor_1 (.a(num2), .b(num1), .out(fpsubtractor_1_out));
  FPMultiplier fpmultiplier_1 (.a(num1), .b(num1), .out(fpmultiplier_1_out));
  FPDivider fpdivider_1 (.a(num2), .b(num1), .out(fpdivider_1_out));
  // FPNegator fpnegator_1: pin names not known; wires that end beside it: num1, fpnegator_1_p2
  Multiplexer #(.select(4), .width(32)) multiplexer_1 (
    .in0(adder_1_out), .in1(subtractor_1_out), .in2(multiplier_1_out), .in3(multiplier_2_out),
    .in4(divider_1_out), .in5(divider_2_out), .in6(negator_1_out), .in7(fpadder_1_out),
    .in8(fpsubtractor_1_out), .in9(fpmultiplier_1_out), .in10(fpdivider_1_out), .in11(fpnegator_1_p2),
    .in12(inttofp_1_p2), .in13(inttofp_2_p2), .in14(fptoint_1_p2), .out(num_out), .sel(instruction));  // open: in15
  Multiplexer #(.select(4)) multiplexer_2 (
    .in0(comparator_1_gt), .in1(comparator_1_eq), .in2(comparator_1_lt), .in3(comparator_2_gt),
    .in4(comparator_2_eq), .in5(comparator_2_lt), .in6(fpcomparator_1_p3), .in7(fpcomparator_1_p4),
    .in8(fpcomparator_1_p5), .in9(1'b0), .in10(1'b0), .in11(1'b0), .in12(1'b0), .in13(1'b0), .in14(1'b0),
    .in15(1'b0), .out(comp_out), .sel(instruction));
endmodule

module instruction_decoder (
  input  [8:0] instruction,
  input  [2:0] sub_stage,
  input  carry,
  input  barrow,
  input  comp,
  output RSC,
  output MA_In,
  output M_I,
  output M_O,
  output IR_I,
  output IR_O,
  output PC_O,
  output PC_Up,
  output PC_jmp,
  output [3:0] ALU_inst,
  output A_I,
  output A_O,
  output N1_I,
  output N1_O,
  output N2_I,
  output N2_O,
  output R0I,
  output R0O,
  output R1I,
  output R1O,
  output R2I,
  output R2O
);
endmodule
